# Fritzing sketch schematic (saved by Fritzing 0.9.3b)

parts:
  GY2 = MPU-6050 Board GY-521 [form="♀ (female)" package=THT]
  Part3 = Adafruit_BMP280
  Raspberry_Pi_Zero1 = Raspberry Pi Zero  # not connected
  Part4 = SO-24x [chip_label=SO-24x package=SO(x)]  # not connected

nets:
  N1: GY2.pin1, Part3.VIN
  N2: GY2.pin3, Part3.SCK/SCL

custom parts:
  MPU-6050 Board GY-521: Acelerometro y Giroscopio MPU-6050 Board GY-521
  Adafruit_BMP280: Bosch has stepped up their game with their new BMP280 sensor, an environmental sensor with temperature, barometric pressure that is the next generation upgrade to the BMP085/BMP180/BMP183. This sensor is great for all sorts of weather sensing and can even be used in both I2C and SPI! This precision sensor from Bosch is the best low-cost, precision sensing solution for measuring barometric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
